// Logisim project brainfuck.circ as structural Verilog: 5 circuits, main circuit brainfuck/cpu
module main (
);

  wire brainfuck_cpu_1_stdin_read, brainfuck_cpu_1_stdout_ready, brainfuck_cpu_1_writing_mem, clk, d_ff_1_q,
       d_ff_2_q, d_ff_3_q;
  wire [2:0] rom_1_data;
  wire [7:0] brainfuck_cpu_1_set_mem, brainfuck_cpu_1_stdout, ram_1_data, register_3_q, register_4_q,
       stdin_out_3;
  wire [23:0] brainfuck_cpu_1_instr_ptr_2, brainfuck_cpu_1_mem_ptr_2, register_1_q, register_2_q;

  ROM #(.addrWidth(24), .dataWidth(3)) rom_1 (.addr(register_1_q), .data(rom_1_data));  // open: sel
  input_stream stdin (.clk(clk), .read(d_ff_3_q), .out_3(stdin_out_3));
  Clock clock_1 (.out(clk));
  brainfuck_cpu brainfuck_cpu_1 (
    .instr(rom_1_data), .instr_ptr(register_1_q), .mem(ram_1_data), .mem_ptr(register_2_q),
    .stdin(stdin_out_3), .instr_ptr_2(brainfuck_cpu_1_instr_ptr_2), .mem_ptr_2(brainfuck_cpu_1_mem_ptr_2),
    .writing_mem(brainfuck_cpu_1_writing_mem), .set_mem(brainfuck_cpu_1_set_mem),
    .stdout_ready(brainfuck_cpu_1_stdout_ready), .stdout(brainfuck_cpu_1_stdout),
    .stdin_read(brainfuck_cpu_1_stdin_read), .clk(clk));
  Register #(.width(24)) register_1 (.D(brainfuck_cpu_1_instr_ptr_2), .Q(register_1_q), .clk(clk));  // open: en, clr
  D_Flip_Flop d_ff_1 (.clk(clk), .D(brainfuck_cpu_1_writing_mem), .Q(d_ff_1_q));  // open: Qn, preset, en, reset
  D_Flip_Flop d_ff_2 (.clk(clk), .D(brainfuck_cpu_1_stdout_ready), .Q(d_ff_2_q));  // open: Qn, preset, en, reset
  D_Flip_Flop d_ff_3 (.clk(clk), .D(brainfuck_cpu_1_stdin_read), .Q(d_ff_3_q));  // open: Qn, preset, en, reset
  Register #(.width(24)) register_2 (.D(brainfuck_cpu_1_mem_ptr_2), .Q(register_2_q), .clk(clk));  // open: en, clr
  Register register_3 (.D(brainfuck_cpu_1_set_mem), .Q(register_3_q), .clk(clk));  // open: en, clr
  Register register_4 (.D(brainfuck_cpu_1_stdout), .Q(register_4_q), .clk(clk));  // open: en, clr
  output_stream stdout (.clk(clk), .writing(d_ff_2_q), .value(register_4_q));
  RAM #(.addrWidth(24), .bus("separate")) ram_1 (
    .addr(register_2_q), .din(register_3_q), .data(ram_1_data), .str(d_ff_1_q), .clk(clk), .ld(1'b1));  // open: sel, clr

  // Notes on the sheet:
  //   contents of rom_1 (hex, n*v repeats v):
  //   7
endmodule

// brainfuck\ncpu
module brainfuck_cpu (
  input  clk,
  input  [2:0] instr,
  input  [23:0] instr_ptr,
  input  [7:0] mem,
  input  [23:0] mem_ptr,
  input  [7:0] stdin,
  output [23:0] instr_ptr_2,
  output [23:0] mem_ptr_2,
  output writing_mem,
  output [7:0] set_mem,
  output stdout_ready,
  output [7:0] stdout,
  output stdin_read
);

  wire and_1_out, and_3_out, input_minus, input_plus, input_t_t, input_t_t_t, input_t_t_t_t, input_t_t_t_t_t,
       or_1_out, skipping;
  wire [1:0] and_5_out;
  wire [5:0] adder_1_out, register_1_q;
  wire [5:5] and_2_out;
  wire [7:0] adder_3_out;

  and and_1 (and_1_out, instr[0], instr[1], instr[2]);
  and and_2 (and_2_out[5], input_t_t_t_t_t, skipping);
  or or_1 (or_1_out, skipping, and_1_out);
  Demultiplexer #(.select(3)) demultiplexer_1 (
    .out0(input_t_t_t), .out1(input_t_t), .out2(input_plus), .out3(input_minus), .out4(stdout_ready),
    .out5(stdin_read), .out6(input_t_t_t_t), .out7(input_t_t_t_t_t), .in(or_1_out), .sel(instr));  // open: en
  or or_2 (skipping, register_1_q[0], register_1_q[1], register_1_q[2], register_1_q[3], register_1_q[4], register_1_q[5]);
  and and_3 (and_3_out, skipping, input_t_t_t_t);
  Adder #(.width(6)) adder_1 (
    .a(register_1_q), .b({6{and_2_out[5]}}), .out(adder_1_out), .cin(and_3_out));  // open: cout
  Register #(.width(6)) register_1 (.D(adder_1_out), .Q(register_1_q), .clk(clk));  // open: en, clr
  // AND_Gate and_4 has open pins: out=and_5_out[1]
  // AND_Gate and_5 has open pins: out=and_5_out[0]
  Adder #(.width(24)) adder_2 (.a(mem_ptr), .b({24{input_t_t}}), .out(mem_ptr_2), .cin(input_t_t_t));  // open: cout
  Adder adder_3 (.a(mem), .b({8{input_minus}}), .out(adder_3_out), .cin(input_plus));  // open: cout
  Multiplexer #(.select(2), .width(24)) multiplexer_1 (
    .in0(instr_ptr), .out(instr_ptr_2), .sel(and_5_out));  // open: in1, in2, in3, en
  or or_3 (writing_mem, input_plus, input_minus, stdin_read);
  Multiplexer #(.width(8)) multiplexer_2 (.in0(adder_3_out), .in1(stdin), .out(set_mem), .sel(stdin_read));  // open: en

  assign stdout = mem;

  // Other names for the same wires on the sheet: input = stdin_read; input_t = stdout_ready
endmodule

module output_stream (
  input  clk,
  input  writing,
  input  [7:0] value
);

  wire [23:0] adder_1_out, register_1_q;

  Register #(.width(24)) register_1 (.D(adder_1_out), .Q(register_1_q), .clk(clk));  // open: en, clr
  Adder #(.width(24)) adder_1 (.a(register_1_q), .b({24{1'b0}}), .out(adder_1_out), .cin(writing));  // open: cout
  RAM #(.addrWidth(24), .bus("separate")) ram_1 (
    .addr(register_1_q), .din(value), .str(writing), .clk(clk));  // open: data, sel, ld, clr
endmodule

module input_stream (
  input  clk,
  input  read,
  output [7:0] out_3
);

  wire [23:0] adder_1_out, register_1_q;

  Adder #(.width(24)) adder_1 (.a(register_1_q), .b({24{1'b0}}), .out(adder_1_out), .cin(read));  // open: cout
  Register #(.width(24)) register_1 (.D(adder_1_out), .Q(register_1_q), .clk(clk));  // open: en, clr
  ROM #(.addrWidth(24)) rom_1 (.addr(register_1_q), .data(out_3));  // open: sel

  // Notes on the sheet:
  //   contents of rom_1 (hex, n*v repeats v):
  //   12 34 f2
endmodule

// Register24\nStack[64]
module Register24Stack64 (
  input  clk,
  input  push,
  input  [23:0] insert_data,
  input  pop,
  output [23:0] tail,
  output err
);

  wire and_1_out, not_1_out, not_2_out, not_3_out, or_1_out, stack_overflow_out, stack_underflow_out;
  wire [5:0] adder_1_out, length_q, subtractor_1_out;
  wire [23:0] multiplexer_1_out;

  not not_1 (not_1_out, push);
  Subtractor #(.width(6)) subtractor_1 (
    .a(length_q), .b({6{1'b0}}), .out(subtractor_1_out), .bin(not_1_out));  // open: bout
  Multiplexer #(.width(24)) multiplexer_1 (
    .in0({24{1'b0}}), .in1(insert_data), .out(multiplexer_1_out), .sel(push));  // open: en
  not not_2 (not_2_out, err);
  not not_3 (not_3_out, or_1_out);
  or or_1 (or_1_out, push, pop);
  Adder #(.width(6)) adder_1 (.a(length_q), .b({6{pop}}), .out(adder_1_out), .cin(push));  // open: cout
  RAM #(.addrWidth(6), .dataWidth(24), .bus("separate")) ram_1 (
    .addr(subtractor_1_out), .din(multiplexer_1_out), .data(tail), .str(or_1_out), .sel(not_2_out),
    .clk(clk), .ld(not_3_out));  // open: clr
  Register #(.width(6)) length (.D(adder_1_out), .Q(length_q), .clk(clk));  // open: en, clr
  and stack_overflow (stack_overflow_out, length_q[0], length_q[1], length_q[2], length_q[3], length_q[4], length_q[5], push);
  and and_1 (and_1_out, push, pop);
  and stack_underflow (stack_underflow_out, ~length_q[0], ~length_q[1], ~length_q[2], ~length_q[3], ~length_q[4], ~length_q[5], pop);  // AND_Gate
  or or_2 (err, stack_overflow_out, and_1_out, stack_underflow_out);
endmodule
